// Logisim project lab2.circ as structural Verilog: 1 circuit, main circuit e2522159
module e2522159 (
  input  O3,
  input  O2,
  input  O1,
  input  O0,
  input  A1,
  input  A0,
  input  B1,
  input  B0,
  output P,
  output Z,
  output L0,
  output L1,
  output L2,
  output L3,
  output L4,
  output L5,
  output L6,
  output L9,
  output E,
  output G,
  output L7,
  output L,
  output L8,
  output S,
  output C
);

  wire and_1_out, and_2_out, and_3_out, and_4_out, n3_to_8_decoder_74138_2_p7, n3_to_8_decoder_74138_3_p7,
       n3_to_8_decoder_74138_3_p8, n3_to_8_decoder_74138_3_p9, n3_to_8_decoder_74138_3_p10,
       n3_to_8_decoder_74138_3_p11, n3_to_8_decoder_74138_3_p12, n3_to_8_decoder_74138_3_p13,
       n3_to_8_decoder_74138_3_p14, not_1_out, not_2_out, not_3_out, not_4_out, not_5_out, not_6_out,
       not_7_out, not_8_out, not_9_out, not_11_out, not_12_out, not_13_out, not_14_out, not_15_out,
       not_17_out, not_18_out, not_19_out, not_20_out, not_21_out, not_22_out, not_23_out, not_24_out,
       not_25_out, not_26_out, not_27_out, not_28_out, not_29_out, not_30_out, not_31_out, not_32_out,
       not_33_out, not_34_out, not_35_out, or_1_out, or_2_out, or_3_out, or_4_out, or_5_out, or_6_out,
       or_7_out, or_8_out, or_9_out, or_10_out, or_11_out, or_12_out, or_13_out, or_14_out, or_15_out,
       or_16_out, or_17_out, or_18_out, or_19_out, or_20_out, or_21_out, or_22_out, or_23_out, or_24_out,
       or_25_out, or_26_out, or_27_out, or_28_out, or_29_out, or_30_out, or_31_out, or_32_out, or_33_out,
       or_34_out, or_35_out, or_36_out, or_37_out, or_38_out, or_39_out, or_40_out, or_41_out, or_42_out,
       or_43_out, or_44_out, or_45_out, or_47_out, or_48_out, or_49_out, or_50_out, or_51_out;

  not not_1 (not_1_out, O3);
  not not_2 (not_2_out, O2);
  not not_3 (not_3_out, O1);
  not not_4 (not_4_out, O0);
  not not_5 (not_5_out, A1);
  not not_6 (not_6_out, A0);
  not not_7 (not_7_out, B1);
  not not_8 (not_8_out, B0);
  or or_1 (or_1_out, or_6_out, or_7_out);
  or or_2 (or_2_out, or_7_out, not_13_out);
  or or_3 (or_3_out, not_23_out, not_20_out);
  and and_1 (and_1_out, A1, A0);
  and and_2 (and_2_out, B1, B0);
  and and_3 (and_3_out, A1, B0);
  and and_4 (and_4_out, A0, B1);
  or or_4 (or_4_out, not_15_out, not_19_out);
  or or_5 (or_5_out, not_22_out, not_18_out);
  // _3_to_8_decoder__74138 #(.Facing("east")) 3_to_8_decoder_74138_1: pin names not known; wires that end beside it: B0, B1, A0, not_4_out
  not not_9 (not_9_out, not_5_out);
  // _3_to_8_decoder__74138 #(.Facing("east")) 3_to_8_decoder_74138_2: pin names not known; wires that end beside it: B0, B1, A0, not_5_out, A1, not_9_out, n3_to_8_decoder_74138_2_p7, not_9_out, n3_to_8_decoder_74138_2_p7
  not not_10 (n3_to_8_decoder_74138_2_p7, A1);
  or or_6 (or_6_out, not_24_out, not_18_out);
  or or_7 (or_7_out, not_19_out, not_13_out);
  or or_8 (or_8_out, or_3_out, or_9_out);
  or or_9 (or_9_out, not_17_out, not_14_out);
  or or_10 (or_10_out, and_1_out, and_2_out);
  or or_11 (or_11_out, and_3_out, and_4_out);
  or or_12 (or_12_out, not_20_out, not_23_out);
  or or_13 (or_13_out, or_4_out, or_12_out);
  or or_14 (or_14_out, or_13_out, or_19_out);
  or or_15 (or_15_out, or_5_out, or_16_out);
  or or_16 (or_16_out, or_17_out, or_20_out);
  or or_17 (or_17_out, not_17_out, not_14_out);
  // NOT_Gate not_11 has open pins: in=open, out=not_11_out
  // NOT_Gate not_12 has open pins: in=open, out=not_12_out
  // NOT_Gate not_13 has open pins: in=open, out=not_13_out
  // NOT_Gate not_14 has open pins: in=open, out=not_14_out
  // NOT_Gate not_15 has open pins: in=open, out=not_15_out
  // NOT_Gate not_16 has open pins: in=open, out=not_13_out
  // NOT_Gate not_17 has open pins: in=open, out=not_17_out
  // NOT_Gate not_18 has open pins: in=open, out=not_18_out
  // NOT_Gate not_19 has open pins: in=open, out=not_19_out
  // NOT_Gate not_20 has open pins: in=open, out=not_20_out
  // NOT_Gate not_21 has open pins: in=open, out=not_21_out
  // NOT_Gate not_22 has open pins: in=open, out=not_22_out
  // NOT_Gate not_23 has open pins: in=open, out=not_23_out
  // NOT_Gate not_24 has open pins: in=open, out=not_24_out
  // NOT_Gate not_25 has open pins: in=open, out=not_25_out
  // NOT_Gate not_26 has open pins: in=open, out=not_26_out
  or or_18 (or_18_out, or_10_out, or_11_out);
  or or_19 (or_19_out, not_24_out, not_25_out);
  or or_20 (or_20_out, not_13_out, not_12_out);
  not not_27 (not_27_out, O3);
  // _3_to_8_decoder__74138 #(.Facing("east")) 3_to_8_decoder_74138_3: pin names not known; wires that end beside it: O0, O1, O2, not_27_out, O3, O3, n3_to_8_decoder_74138_3_p7, n3_to_8_decoder_74138_3_p8, n3_to_8_decoder_74138_3_p9, n3_to_8_decoder_74138_3_p10, n3_to_8_decoder_74138_3_p11, n3_to_8_decoder_74138_3_p12, n3_to_8_decoder_74138_3_p13, n3_to_8_decoder_74138_3_p14
  not not_28 (not_28_out, n3_to_8_decoder_74138_3_p7);
  assign L0 = not_28_out ? not_5_out : 1'bz;  // Controlled_Buffer controlled_buffer_1
  assign L1 = not_28_out ? not_8_out : 1'bz;  // Controlled_Buffer controlled_buffer_2
  assign L2 = not_28_out ? not_22_out : 1'bz;  // Controlled_Buffer controlled_buffer_3
  assign L3 = not_28_out ? 1'b0 : 1'bz;  // Controlled_Buffer controlled_buffer_4
  assign L4 = not_28_out ? 1'b0 : 1'bz;  // Controlled_Buffer controlled_buffer_5
  assign L5 = not_28_out ? 1'b0 : 1'bz;  // Controlled_Buffer controlled_buffer_6
  assign L6 = not_28_out ? 1'b0 : 1'bz;  // Controlled_Buffer controlled_buffer_7
  assign L9 = not_28_out ? 1'b0 : 1'bz;  // Controlled_Buffer controlled_buffer_8
  or or_21 (or_21_out, not_11_out, not_26_out);
  or or_22 (or_22_out, not_13_out, not_21_out);
  assign E = not_28_out ? 1'b0 : 1'bz;  // Controlled_Buffer controlled_buffer_9
  assign G = not_28_out ? 1'b0 : 1'bz;  // Controlled_Buffer controlled_buffer_10
  assign L = not_28_out ? 1'b0 : 1'bz;  // Controlled_Buffer controlled_buffer_11
  or or_23 (or_23_out, not_12_out, not_13_out);
  or or_24 (or_24_out, not_14_out, not_17_out);
  or or_25 (or_25_out, not_18_out, not_22_out);
  assign S = not_28_out ? 1'b0 : 1'bz;  // Controlled_Buffer controlled_buffer_12
  or or_26 (or_26_out, not_18_out, not_21_out);
  or or_27 (or_27_out, not_22_out, not_24_out);
  or or_28 (or_28_out, not_25_out, not_26_out);
  assign C = not_28_out ? 1'b0 : 1'bz;  // Controlled_Buffer controlled_buffer_13
  not not_29 (not_29_out, n3_to_8_decoder_74138_3_p8);
  assign L0 = not_29_out ? not_6_out : 1'bz;  // Controlled_Buffer controlled_buffer_14
  assign L1 = not_29_out ? 1'b0 : 1'bz;  // Controlled_Buffer controlled_buffer_15
  assign L2 = not_29_out ? or_29_out : 1'bz;  // Controlled_Buffer controlled_buffer_16
  or or_29 (or_29_out, not_20_out, not_17_out);
  or or_30 (or_30_out, not_18_out, not_24_out);
  assign L3 = not_29_out ? or_30_out : 1'bz;  // Controlled_Buffer controlled_buffer_17
  assign L4 = not_29_out ? not_21_out : 1'bz;  // Controlled_Buffer controlled_buffer_18
  assign L5 = not_29_out ? 1'b0 : 1'bz;  // Controlled_Buffer controlled_buffer_19
  or or_31 (or_31_out, not_22_out, not_25_out);
  assign L6 = not_29_out ? or_31_out : 1'bz;  // Controlled_Buffer controlled_buffer_20
  assign L9 = not_29_out ? not_26_out : 1'bz;  // Controlled_Buffer controlled_buffer_21
  assign E = not_29_out ? 1'b0 : 1'bz;  // Controlled_Buffer controlled_buffer_22
  assign G = not_29_out ? 1'b0 : 1'bz;  // Controlled_Buffer controlled_buffer_23
  assign L = not_29_out ? 1'b0 : 1'bz;  // Controlled_Buffer controlled_buffer_24
  assign S = not_29_out ? 1'b0 : 1'bz;  // Controlled_Buffer controlled_buffer_25
  assign C = not_29_out ? 1'b0 : 1'bz;  // Controlled_Buffer controlled_buffer_26
  or or_32 (or_32_out, or_23_out, or_24_out);
  or or_33 (or_33_out, or_26_out, or_27_out);
  not not_30 (not_30_out, n3_to_8_decoder_74138_3_p9);
  assign L0 = not_30_out ? B1 : 1'bz;  // Controlled_Buffer controlled_buffer_27
  assign L1 = not_30_out ? 1'b0 : 1'bz;  // Controlled_Buffer controlled_buffer_28
  assign L2 = not_30_out ? not_20_out : 1'bz;  // Controlled_Buffer controlled_buffer_29
  assign L3 = not_30_out ? not_24_out : 1'bz;  // Controlled_Buffer controlled_buffer_30
  assign L4 = not_30_out ? 1'b0 : 1'bz;  // Controlled_Buffer controlled_buffer_31
  assign L5 = not_30_out ? 1'b0 : 1'bz;  // Controlled_Buffer controlled_buffer_32
  assign L6 = not_30_out ? 1'b0 : 1'bz;  // Controlled_Buffer controlled_buffer_33
  assign L9 = not_30_out ? 1'b0 : 1'bz;  // Controlled_Buffer controlled_buffer_34
  assign E = not_30_out ? 1'b0 : 1'bz;  // Controlled_Buffer controlled_buffer_35
  assign G = not_30_out ? 1'b0 : 1'bz;  // Controlled_Buffer controlled_buffer_36
  assign L = not_30_out ? 1'b0 : 1'bz;  // Controlled_Buffer controlled_buffer_37
  or or_34 (or_34_out, or_32_out, or_25_out);
  assign S = not_30_out ? 1'b0 : 1'bz;  // Controlled_Buffer controlled_buffer_38
  or or_35 (or_35_out, or_33_out, or_28_out);
  assign C = not_30_out ? 1'b0 : 1'bz;  // Controlled_Buffer controlled_buffer_39
  not not_31 (not_31_out, n3_to_8_decoder_74138_3_p10);
  assign L0 = not_31_out ? not_6_out : 1'bz;  // Controlled_Buffer controlled_buffer_40
  assign L1 = not_31_out ? 1'b0 : 1'bz;  // Controlled_Buffer controlled_buffer_41
  assign L2 = not_31_out ? or_2_out : 1'bz;  // Controlled_Buffer controlled_buffer_42
  assign L3 = not_31_out ? or_8_out : 1'bz;  // Controlled_Buffer controlled_buffer_43
  or or_36 (or_36_out, not_21_out, not_18_out);
  assign L4 = not_31_out ? or_37_out : 1'bz;  // Controlled_Buffer controlled_buffer_44
  or or_37 (or_37_out, or_36_out, not_24_out);
  or or_38 (or_38_out, not_22_out, not_25_out);
  assign L5 = not_31_out ? or_38_out : 1'bz;  // Controlled_Buffer controlled_buffer_45
  assign L6 = not_31_out ? not_26_out : 1'bz;  // Controlled_Buffer controlled_buffer_46
  assign L9 = not_31_out ? 1'b0 : 1'bz;  // Controlled_Buffer controlled_buffer_47
  assign E = not_31_out ? 1'b0 : 1'bz;  // Controlled_Buffer controlled_buffer_48
  assign G = not_31_out ? 1'b0 : 1'bz;  // Controlled_Buffer controlled_buffer_49
  assign L = not_31_out ? 1'b0 : 1'bz;  // Controlled_Buffer controlled_buffer_50
  assign S = not_31_out ? 1'b0 : 1'bz;  // Controlled_Buffer controlled_buffer_51
  assign C = not_31_out ? or_35_out : 1'bz;  // Controlled_Buffer controlled_buffer_52
  not not_32 (not_32_out, n3_to_8_decoder_74138_3_p11);
  assign L0 = not_32_out ? or_39_out : 1'bz;  // Controlled_Buffer controlled_buffer_53
  or or_39 (or_39_out, not_26_out, not_11_out);
  or or_40 (or_40_out, not_20_out, not_12_out);
  assign L1 = not_32_out ? or_40_out : 1'bz;  // Controlled_Buffer controlled_buffer_54
  assign L2 = not_32_out ? or_1_out : 1'bz;  // Controlled_Buffer controlled_buffer_55
  assign L3 = not_32_out ? or_41_out : 1'bz;  // Controlled_Buffer controlled_buffer_56
  buf or_41 (or_41_out, not_14_out);  // OR_Gate
  assign L4 = not_32_out ? 1'b0 : 1'bz;  // Controlled_Buffer controlled_buffer_57
  assign L5 = not_32_out ? 1'b0 : 1'bz;  // Controlled_Buffer controlled_buffer_58
  assign L6 = not_32_out ? 1'b0 : 1'bz;  // Controlled_Buffer controlled_buffer_59
  assign L9 = not_32_out ? 1'b0 : 1'bz;  // Controlled_Buffer controlled_buffer_60
  assign E = not_32_out ? 1'b0 : 1'bz;  // Controlled_Buffer controlled_buffer_61
  assign G = not_32_out ? 1'b0 : 1'bz;  // Controlled_Buffer controlled_buffer_62
  assign L = not_32_out ? 1'b0 : 1'bz;  // Controlled_Buffer controlled_buffer_63
  assign S = not_32_out ? or_34_out : 1'bz;  // Controlled_Buffer controlled_buffer_64
  assign C = not_32_out ? 1'b0 : 1'bz;  // Controlled_Buffer controlled_buffer_65
  or or_42 (or_42_out, or_21_out, or_22_out);
  not not_33 (not_33_out, n3_to_8_decoder_74138_3_p12);
  assign L0 = not_33_out ? 1'b0 : 1'bz;  // Controlled_Buffer controlled_buffer_66
  assign L1 = not_33_out ? 1'b0 : 1'bz;  // Controlled_Buffer controlled_buffer_67
  assign L2 = not_33_out ? 1'b0 : 1'bz;  // Controlled_Buffer controlled_buffer_68
  assign L3 = not_33_out ? 1'b0 : 1'bz;  // Controlled_Buffer controlled_buffer_69
  assign L4 = not_33_out ? 1'b0 : 1'bz;  // Controlled_Buffer controlled_buffer_70
  assign L5 = not_33_out ? 1'b0 : 1'bz;  // Controlled_Buffer controlled_buffer_71
  assign L6 = not_33_out ? 1'b0 : 1'bz;  // Controlled_Buffer controlled_buffer_72
  assign L9 = not_33_out ? 1'b0 : 1'bz;  // Controlled_Buffer controlled_buffer_73
  assign E = not_33_out ? or_42_out : 1'bz;  // Controlled_Buffer controlled_buffer_74
  assign G = not_33_out ? or_14_out : 1'bz;  // Controlled_Buffer controlled_buffer_75
  assign L = not_33_out ? or_15_out : 1'bz;  // Controlled_Buffer controlled_buffer_76
  assign S = not_33_out ? 1'b0 : 1'bz;  // Controlled_Buffer controlled_buffer_77
  assign C = not_33_out ? 1'b0 : 1'bz;  // Controlled_Buffer controlled_buffer_78
  not not_34 (not_34_out, n3_to_8_decoder_74138_3_p13);
  assign L0 = not_34_out ? not_7_out : 1'bz;  // Controlled_Buffer controlled_buffer_79
  assign L1 = not_34_out ? not_18_out : 1'bz;  // Controlled_Buffer controlled_buffer_80
  assign L2 = not_34_out ? or_48_out : 1'bz;  // Controlled_Buffer controlled_buffer_81
  assign L3 = not_34_out ? not_26_out : 1'bz;  // Controlled_Buffer controlled_buffer_82
  assign L4 = not_34_out ? 1'b0 : 1'bz;  // Controlled_Buffer controlled_buffer_83
  assign L5 = not_34_out ? 1'b0 : 1'bz;  // Controlled_Buffer controlled_buffer_84
  assign L6 = not_34_out ? 1'b0 : 1'bz;  // Controlled_Buffer controlled_buffer_85
  assign L9 = not_34_out ? 1'b0 : 1'bz;  // Controlled_Buffer controlled_buffer_86
  assign E = not_34_out ? 1'b0 : 1'bz;  // Controlled_Buffer controlled_buffer_87
  assign G = not_34_out ? 1'b0 : 1'bz;  // Controlled_Buffer controlled_buffer_88
  assign L = not_34_out ? 1'b0 : 1'bz;  // Controlled_Buffer controlled_buffer_89
  assign S = not_34_out ? 1'b0 : 1'bz;  // Controlled_Buffer controlled_buffer_90
  assign C = not_34_out ? 1'b0 : 1'bz;  // Controlled_Buffer controlled_buffer_91
  not not_35 (not_35_out, n3_to_8_decoder_74138_3_p14);
  or or_43 (or_43_out, not_26_out, not_11_out);
  assign L0 = not_35_out ? or_43_out : 1'bz;  // Controlled_Buffer controlled_buffer_92
  assign L1 = not_35_out ? not_12_out : 1'bz;  // Controlled_Buffer controlled_buffer_93
  assign L2 = not_35_out ? or_47_out : 1'bz;  // Controlled_Buffer controlled_buffer_94
  assign L3 = not_35_out ? or_8_out : 1'bz;  // Controlled_Buffer controlled_buffer_95
  assign L4 = not_35_out ? 1'b0 : 1'bz;  // Controlled_Buffer controlled_buffer_96
  assign L5 = not_35_out ? 1'b0 : 1'bz;  // Controlled_Buffer controlled_buffer_97
  assign L6 = not_35_out ? 1'b0 : 1'bz;  // Controlled_Buffer controlled_buffer_98
  assign L9 = not_35_out ? 1'b0 : 1'bz;  // Controlled_Buffer controlled_buffer_99
  assign E = not_35_out ? 1'b0 : 1'bz;  // Controlled_Buffer controlled_buffer_100
  assign G = not_35_out ? 1'b0 : 1'bz;  // Controlled_Buffer controlled_buffer_101
  assign L = not_35_out ? 1'b0 : 1'bz;  // Controlled_Buffer controlled_buffer_102
  assign S = not_35_out ? 1'b0 : 1'bz;  // Controlled_Buffer controlled_buffer_103
  assign C = not_35_out ? 1'b0 : 1'bz;  // Controlled_Buffer controlled_buffer_104
  or or_44 (or_44_out, L1, L2);
  assign L0 = O3 ? not_11_out : 1'bz;  // Controlled_Buffer controlled_buffer_105
  assign L1 = O3 ? not_12_out : 1'bz;  // Controlled_Buffer controlled_buffer_106
  or or_45 (or_45_out, not_19_out, not_21_out);
  assign L2 = O3 ? or_45_out : 1'bz;  // Controlled_Buffer controlled_buffer_107
  assign L3 = O3 ? or_18_out : 1'bz;  // Controlled_Buffer controlled_buffer_108
  assign L4 = O3 ? 1'b0 : 1'bz;  // Controlled_Buffer controlled_buffer_109
  assign L5 = O3 ? 1'b0 : 1'bz;  // Controlled_Buffer controlled_buffer_110
  assign L6 = O3 ? 1'b0 : 1'bz;  // Controlled_Buffer controlled_buffer_111
  assign L9 = O3 ? 1'b0 : 1'bz;  // Controlled_Buffer controlled_buffer_112
  assign E = O3 ? 1'b0 : 1'bz;  // Controlled_Buffer controlled_buffer_113
  assign G = O3 ? 1'b0 : 1'bz;  // Controlled_Buffer controlled_buffer_114
  assign L = O3 ? 1'b0 : 1'bz;  // Controlled_Buffer controlled_buffer_115
  assign S = O3 ? 1'b0 : 1'bz;  // Controlled_Buffer controlled_buffer_116
  assign C = O3 ? 1'b0 : 1'bz;  // Controlled_Buffer controlled_buffer_117
  or or_46 (P, or_44_out, L4);
  or or_47 (or_47_out, or_49_out, or_50_out);
  or or_48 (or_48_out, not_21_out, or_51_out);
  or or_49 (or_49_out, not_24_out, not_19_out);
  or or_50 (or_50_out, not_18_out, not_13_out);
  or or_51 (or_51_out, not_22_out, not_25_out);

  assign L7 = 1'b0;
  assign L8 = 1'b0;
  assign Z = L0;
endmodule
